# Fritzing sketch Temp-Humid Board BME280 (saved by Fritzing 0.9.3b)
circuit board: 7cm x 5cm
breadboards: 1

parts:
  S1 = Pushbutton [package="[SMD]"]
  Part1 = GY-VL53L0Xv2 Time of Flight Distance Sensor [part_number=CJVL53L0Xv2]
  LCM1602_IIC1 = LCM1602 IIC [part_number="LCM1602 IIC" chip_label="LCM1602 IIC" package="DIP (Dual Inline) [THT]"]
  LCD1 = LCD screen
  Raspberry_Pi_3 = Raspberry Pi 3 [part_number=RPI-3-V1.2]
  GY-BMP280 = GY-BMEP280 Barometric Pressure Sensor - Breakout

nets:
  GND: S1.Pin_1, S1.Pin_2, Part1.GND, Raspberry_Pi_3.GND, GY-BMP280.GND
  N1: S1.Pin_3, S1.Pin_4, Raspberry_Pi_3.GPIO17
  VCC: Part1.VCC, Raspberry_Pi_3.3v3, GY-BMP280.VCC
  N2: Part1.SCL, LCM1602_IIC1.SDA, Raspberry_Pi_3.GPIO3, GY-BMP280.SCL
  N3: Part1.SDA, LCM1602_IIC1.SCL, Raspberry_Pi_3.GPIO2, GY-BMP280.SDA
  VSS: LCM1602_IIC1.VSS, LCD1.VSS
  VDD: LCM1602_IIC1.VDD, LCD1.VDD
  N4: LCM1602_IIC1.V0, LCD1.V0
  N5: LCM1602_IIC1.RS, LCD1.RS
  N6: LCM1602_IIC1.RW, LCD1.R/W
  N7: LCM1602_IIC1.E, LCD1.E
  N8: LCM1602_IIC1.D0, LCD1.DB0
  N9: LCM1602_IIC1.D1, LCD1.DB1
  N10: LCM1602_IIC1.D2, LCD1.DB2
  N11: LCM1602_IIC1.D3, LCD1.DB3
  N12: LCM1602_IIC1.D4, LCD1.DB4
  N13: LCM1602_IIC1.D5, LCD1.DB5
  N14: LCM1602_IIC1.D6, LCD1.DB6
  N15: LCM1602_IIC1.D7, LCD1.DB7
  N16: LCM1602_IIC1.A, LCD1.LED+
  N17: LCM1602_IIC1.K, LCD1.LED-
  N18: LCM1602_IIC1.GND, GY-BMP280.CSB
  VCC_2: LCM1602_IIC1.VCC, Raspberry_Pi_3.5V
  N19: LCM1602_IIC1.LED_A, LCM1602_IIC1.LED_B

custom parts:
  GY-VL53L0Xv2 Time of Flight Distance Sensor: The VL53L0X is a Time of Flight distance sensor like no other you've used! The sensor contains a very tiny invisible laser source, and a matching sensor. The VL53L0X can detect the "time of flight", or how long the light has taken to bounce back to the sensor. Since it uses a very narrow light source, it is good for determining distance of only the surface directly in front of it. Unlike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
  LCM1602 IIC: I2C-Module to use a 1602 or 2004 LCD on with the wire.h libory Serial LCD Modul
  GY-BMEP280 Barometric Pressure Sensor - Breakout: The BME280 is a chip which was originally designed for the next generation of smartphones. It is made up of a very accurate pressure sensor and an associated temperature sensor which helps calibrate the pressure readings. And just for fun they threw in a pretty solid humidity sensor in there as well! So with an I2C connection you have access to enough weather data to make some pretty good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
